// Logisim project BC.circ as structural Verilog
module main (
  input  [7:0] INP,
  output out_2,
  output out_3,
  output [7:0] out_4,
  output [15:0] out_5,
  output [7:0] out_6,
  output [15:0] out_7,
  output [15:0] out_8,
  output [15:0] out_9,
  output [15:0] out_10,
  output out_11,
  output [7:0] out_12,
  output [11:0] out_13,
  output [15:0] out_14,
  output [15:0] out_15,
  output [15:0] out_16,
  output [15:0] out_17
);

  wire CLK, CLOCK_out, FGI, FGO, HLT, I, IEN, j_k_ff_1_q, memory_1_ld, memory_1_out_5;

  R r_1 (.FGO(FGO), .FGI(FGI), .IEN(IEN), .SC(out_4), .CLK(CLK), .OUT(out_2));
  OUTR outr_1 (.INS(out_12), .ADDRESS(out_13), .SC(out_4), .I(I), .OUT(out_6), .BUS_IN(out_17), .CLK(CLK));
  and HALT (HLT, out_13[0], ~I, out_12[7], out_4[3]);  // AND_Gate
  E e_1 (.INS(out_12), .SC(out_4), .ADDRESS(out_13), .I(I), .CLK(CLK), .Cout(out_11), .E(out_3));
  Clock CLOCK (.out(CLOCK_out));
  and and_1 (CLK, CLOCK_out, j_k_ff_1_q);
  IEN ien_1 (.INS(out_12), .SC(out_4), .CLK(CLK), .ADDRESS(out_13), .I(I), .OUT(IEN), .R(out_2));
  control_SC control_sc_1 (.INS(out_12), .R(out_2), .CLK(CLK), .SC(out_4));
  J_K_Flip_Flop j_k_ff_1 (.J(1'b0), .clk(CLOCK_out), .K(HLT), .Q(j_k_ff_1_q));  // open: Qn, preset, en, reset
  ALU alu_1 (
    .E_IN(out_3), .AC(out_10), .DR(out_8), .I(I), .INPR(INP), .SC(out_4), .INS(out_12), .ADDRESS(out_13),
    .ALU_OUT(out_9), .ALU_Cout(out_11));
  FGI fgi_1 (.ADDRESS(out_13), .CLK(CLK), .INS(out_12), .SC(out_4), .INPR(INP), .I(I), .OUT(FGI));
  control_DR control_dr_1 (.BUS_IN(out_17), .BUS_OUT(out_8), .CLK(CLK), .INS(out_12), .SC(out_4));
  FGO fgo_1 (.ADDRESS(out_13), .CLK(CLK), .INS(out_12), .SC(out_4), .I(I), .OUT(FGO));
  control_AC control_ac_1 (
    .ALU_IN(out_9), .BUS_OUT(out_10), .CLK(CLK), .INS(out_12), .SC(out_4), .ADDRESS(out_13), .I(I));
  control_IR control_ir_1 (
    .BUS_IN(out_17), .R(out_2), .ADDRESS(out_13), .I(I), .INSTRUCTION(out_12), .SC(out_4), .CLK(CLK),
    .BUS_OUT(out_14));
  control_TR control_tr_1 (.BUS_IN(out_17), .R(out_2), .BUS_OUT(out_15), .CLK(CLK), .SC(out_4));
  control_AR control_ar_1 (.OUT(out_5), .CLK(CLK), .I(I), .BUS_IN(out_17), .IR_INS(out_12), .SC(out_4), .R(out_2));
  control_PC control_pc_1 (
    .E(out_3), .FGI(FGI), .FGO(FGO), .DR(out_8), .BUS_IN(out_17), .BUS_OUT(out_7), .CLK(CLK), .R(out_2),
    .ADDRESS(out_13), .I(I), .INS(out_12), .SC(out_4), .AC(out_10));
  RAM #(.addrWidth(12), .dataWidth(16), .bus("separate")) ram_1 (
    .addr(out_5[11:0]), .din(out_17), .data(out_16), .str(memory_1_out_5), .clk(CLK), .ld(memory_1_ld));  // open: sel, clr
  Memory memory_1 (.R(out_2), .I(I), .out_5(memory_1_out_5), .SC(out_4), .INS(out_12), .LD(memory_1_ld));
  BUS bus_1 (
    .I(I), .INS(out_12), .SC(out_4), .ADDRESS(out_13), .R(out_2), .AR(out_5), .PC(out_7), .DR(out_8),
    .AC(out_10), .IR(out_14), .TR(out_15), .Mem(out_16), .BUS_OUT(out_17));

  // Other names for the same wires on the sheet: AC[15:0] = out_10; ADDRESS[11:0] = out_13; AR[11:0] = out_5[11:0];
  //   BUS[15:0] = out_17; Cout = out_11; DR[15:0] = out_8; E = out_3; INSTRUCTION[7:0] = out_12; OUTR[7:0] = out_6;
  //   R = out_2; T[7:0] = out_4
endmodule

module AR (
  input  CLR,
  input  INC,
  input  LD,
  input  [15:0] IN,
  input  CLK,
  output [15:0] OUT
);

  wire or_1_out;
  wire [11:0] multiplexer_1_out, n12_bit_adder_1_sum;

  _12_Bit_ADDER u_12_bit_adder_1 (.SUM(n12_bit_adder_1_sum), .B(12'h1), .A(OUT[11:0]), .Cin(1'b0));  // open: Cout
  Multiplexer #(.width(12), .enable("false")) multiplexer_1 (
    .in0(IN[11:0]), .in1(n12_bit_adder_1_sum), .out(multiplexer_1_out), .sel(INC));
  or or_1 (or_1_out, LD, INC);
  Register #(.width(12)) register_1 (.D(multiplexer_1_out), .en(or_1_out), .Q(OUT[11:0]), .clk(CLK), .clr(CLR));

  assign OUT[15:12] = 4'b0000;
endmodule

module PC (
  input  CLR,
  input  INC,
  input  LD,
  input  [15:0] IN,
  input  CLK,
  output [15:0] OUT
);

  wire or_1_out;
  wire [11:0] multiplexer_1_out, n12_bit_adder_1_sum;

  _12_Bit_ADDER u_12_bit_adder_1 (.SUM(n12_bit_adder_1_sum), .B(12'h1), .A(OUT[11:0]), .Cin(1'b0));  // open: Cout
  Multiplexer #(.width(12), .enable("false")) multiplexer_1 (
    .in0(IN[11:0]), .in1(n12_bit_adder_1_sum), .out(multiplexer_1_out), .sel(INC));
  or or_1 (or_1_out, LD, INC);
  Register #(.width(12)) register_1 (.D(multiplexer_1_out), .en(or_1_out), .Q(OUT[11:0]), .clk(CLK), .clr(CLR));

  assign OUT[15:12] = 4'b0000;
endmodule

module IR (
  input  [15:0] BUS_IN,
  input  LD,
  input  CLK,
  output [11:0] ADDRESS,
  output [7:0] INSTRUCTION,
  output I,
  output [15:0] BUS_OUT
);

  Register #(.width(16)) register_1 (.D(BUS_IN), .en(LD), .Q({BUS_OUT[15:12], ADDRESS}), .clk(CLK));  // open: clr
  Decoder #(.select(3), .enable("false")) decoder_1 (
    .out0(INSTRUCTION[0]), .out1(INSTRUCTION[1]), .out2(INSTRUCTION[2]), .out3(INSTRUCTION[3]),
    .out4(INSTRUCTION[4]), .out5(INSTRUCTION[5]), .out6(INSTRUCTION[6]), .out7(INSTRUCTION[7]),
    .sel(BUS_OUT[14:12]));

  assign BUS_OUT[11:0] = ADDRESS;
  assign I = BUS_OUT[15];
endmodule

module DR (
  input  [15:0] BUS_IN,
  input  LD,
  input  INC,
  input  CLK,
  input  CLR,
  output [15:0] BUS_OUT
);

  wire or_1_out;
  wire [15:0] multiplexer_1_out, n16_bit_adder_1_sum;

  _16_Bit_ADDER u_16_bit_adder_1 (.SUM(n16_bit_adder_1_sum), .B(16'h1), .A(BUS_OUT), .Cin(1'b0));  // open: Cout
  Multiplexer #(.width(16), .enable("false")) multiplexer_1 (
    .in0(BUS_IN), .in1(n16_bit_adder_1_sum), .out(multiplexer_1_out), .sel(INC));
  or or_1 (or_1_out, LD, INC);
  Register #(.width(16), .trigger("falling")) register_1 (
    .D(multiplexer_1_out), .en(or_1_out), .Q(BUS_OUT), .clk(CLK), .clr(CLR));
endmodule

module TR (
  input  [15:0] BUS_IN,
  input  LD,
  input  INC,
  input  CLK,
  input  CLR,
  output [15:0] BUS_OUT
);

  wire or_1_out;
  wire [15:0] multiplexer_1_out, n16_bit_adder_1_sum;

  _16_Bit_ADDER u_16_bit_adder_1 (.SUM(n16_bit_adder_1_sum), .B(16'h1), .A(BUS_OUT), .Cin(1'b0));  // open: Cout
  Multiplexer #(.width(16), .enable("false")) multiplexer_1 (
    .in0(BUS_IN), .in1(n16_bit_adder_1_sum), .out(multiplexer_1_out), .sel(INC));
  or or_1 (or_1_out, LD, INC);
  Register #(.width(16)) register_1 (.D(multiplexer_1_out), .en(or_1_out), .Q(BUS_OUT), .clk(CLK), .clr(CLR));
endmodule

module AC (
  input  [15:0] ALU_IN,
  input  INC,
  input  LD,
  input  CLK,
  input  CLR,
  output [15:0] BUS_OUT
);

  wire [15:0] multiplexer_1_out, n16_bit_adder_1_sum;

  _16_Bit_ADDER u_16_bit_adder_1 (.SUM(n16_bit_adder_1_sum), .B(16'h1), .A(BUS_OUT), .Cin(1'b0));  // open: Cout
  // Probe on n16_bit_adder_1_sum
  Multiplexer #(.width(16), .enable("false")) multiplexer_1 (
    .in0(ALU_IN), .in1(n16_bit_adder_1_sum), .out(multiplexer_1_out), .sel(INC));
  Register #(.width(16), .trigger("falling")) register_1 (
    .D(multiplexer_1_out), .en(LD), .Q(BUS_OUT), .clk(CLK), .clr(CLR));
endmodule

// SC
module Sequence_Counter (
  input  CLK,
  input  CLR,
  output [7:0] OUT
);

  wire and_1_out, or_1_out;
  wire [2:0] adder_1_out, register_1_q;

  Register #(.width(3)) register_1 (.D(adder_1_out), .Q(register_1_q), .clk(CLK), .clr(or_1_out));  // open: en
  or or_1 (or_1_out, CLR, and_1_out);
  and and_1 (and_1_out, register_1_q[2], register_1_q[1], register_1_q[0]);
  Adder #(.width(3)) adder_1 (.a(3'b001), .b(register_1_q), .out(adder_1_out), .cin(1'b0));  // open: cout
  Decoder #(.select(3), .enable("false")) decoder_1 (
    .out0(OUT[0]), .out1(OUT[1]), .out2(OUT[2]), .out3(OUT[3]), .out4(OUT[4]), .out5(OUT[5]), .out6(OUT[6]),
    .out7(OUT[7]), .sel(register_1_q));
endmodule

// 1ADD
module _1_Bit_ADDER (
  input  Cin,
  input  Ai,
  input  Bi,
  output SUM,
  output Cout
);

  wire and_1_out, and_2_out, xor_1_out;

  xor xor_1 (xor_1_out, Ai, Bi);
  xor xor_2 (SUM, Cin, xor_1_out);
  and and_1 (and_1_out, xor_1_out, Cin);
  and and_2 (and_2_out, Bi, Ai);
  or or_1 (Cout, and_1_out, and_2_out);
endmodule

// 4ADD
module _4_Bit_ADDER (
  input  [3:0] A,
  input  Cin,
  input  [3:0] B,
  output [3:0] SUM,
  output Cout
);

  wire n1_bit_adder_1_cout, n1_bit_adder_2_cout, n1_bit_adder_3_cout;

  _1_Bit_ADDER u_1_bit_adder_1 (.Ai(A[0]), .Bi(B[0]), .SUM(SUM[0]), .Cout(n1_bit_adder_1_cout), .Cin(Cin));
  _1_Bit_ADDER u_1_bit_adder_2 (
    .Ai(A[1]), .Bi(B[1]), .SUM(SUM[1]), .Cout(n1_bit_adder_2_cout), .Cin(n1_bit_adder_1_cout));
  _1_Bit_ADDER u_1_bit_adder_3 (
    .Ai(A[2]), .Bi(B[2]), .SUM(SUM[2]), .Cout(n1_bit_adder_3_cout), .Cin(n1_bit_adder_2_cout));
  _1_Bit_ADDER u_1_bit_adder_4 (.Ai(A[3]), .Bi(B[3]), .SUM(SUM[3]), .Cout(Cout), .Cin(n1_bit_adder_3_cout));
endmodule

// 12ADD
module _12_Bit_ADDER (
  input  [11:0] B,
  input  [11:0] A,
  input  Cin,
  output [11:0] SUM,
  output Cout
);

  wire n4_bit_adder_1_cout, n4_bit_adder_2_cout;

  _4_Bit_ADDER u_4_bit_adder_1 (.SUM(SUM[3:0]), .B(B[3:0]), .A(A[3:0]), .Cin(Cin), .Cout(n4_bit_adder_1_cout));
  _4_Bit_ADDER u_4_bit_adder_2 (
    .SUM(SUM[7:4]), .B(B[7:4]), .A(A[7:4]), .Cin(n4_bit_adder_1_cout), .Cout(n4_bit_adder_2_cout));
  _4_Bit_ADDER u_4_bit_adder_3 (.SUM(SUM[11:8]), .B(B[11:8]), .A(A[11:8]), .Cin(n4_bit_adder_2_cout), .Cout(Cout));
endmodule

// FA
module _16_Bit_ADDER (
  input  [15:0] B,
  input  [15:0] A,
  input  Cin,
  output [15:0] SUM,
  output Cout
);

  wire n12_bit_adder_1_cout;

  _12_Bit_ADDER u_12_bit_adder_1 (.SUM(SUM[11:0]), .B(B[11:0]), .A(A[11:0]), .Cin(Cin), .Cout(n12_bit_adder_1_cout));
  _4_Bit_ADDER u_4_bit_adder_1 (.SUM(SUM[15:12]), .B(B[15:12]), .A(A[15:12]), .Cin(n12_bit_adder_1_cout), .Cout(Cout));
endmodule

// AR
module control_AR (
  input  I,
  input  [15:0] BUS_IN,
  input  CLK,
  input  [7:0] IR_INS,
  input  [7:0] SC,
  input  R,
  output [15:0] OUT
);

  wire D5T4_out, D7_prime_IT3_out, not_1_out, not_2_out, or_1_out, R_prime_T0_out, R_prime_T2_out, RT0_out;

  not not_1 (not_1_out, IR_INS[7]);
  and D7_prime_IT3 (D7_prime_IT3_out, I, SC[3], not_1_out);
  and R_prime_T2 (R_prime_T2_out, SC[2], not_2_out);
  and R_prime_T0 (R_prime_T0_out, SC[0], not_2_out);
  or or_1 (or_1_out, D7_prime_IT3_out, R_prime_T2_out, R_prime_T0_out);
  not not_2 (not_2_out, R);
  and D5T4 (D5T4_out, IR_INS[5], SC[4]);
  and RT0 (RT0_out, SC[0], R);
  AR ar_1 (.IN(BUS_IN), .CLK(CLK), .OUT(OUT), .CLR(RT0_out), .INC(D5T4_out), .LD(or_1_out));
endmodule

// IR
module control_IR (
  input  [15:0] BUS_IN,
  input  CLK,
  input  R,
  input  [7:0] SC,
  output [7:0] INSTRUCTION,
  output I,
  output [11:0] ADDRESS,
  output [15:0] BUS_OUT
);

  wire and_1_out, not_1_out;

  and and_1 (and_1_out, not_1_out, SC[1]);
  not not_1 (not_1_out, R);
  IR ir_1 (
    .BUS_IN(BUS_IN), .ADDRESS(ADDRESS), .LD(and_1_out), .CLK(CLK), .I(I), .INSTRUCTION(INSTRUCTION),
    .BUS_OUT(BUS_OUT));
endmodule

// PC
module control_PC (
  input  R,
  input  [15:0] BUS_IN,
  input  CLK,
  input  E,
  input  FGI,
  input  FGO,
  input  I,
  input  [15:0] AC,
  input  [7:0] INS,
  input  [7:0] SC,
  input  [15:0] DR,
  input  [11:0] ADDRESS,
  output [15:0] BUS_OUT
);

  wire D4T4_out, D5T5_out, DR_prime_D6T6_out, nor_1_out, nor_2_out, not_1_out, not_2_out, not_3_out,
       not_4_out, or_1_out, or_2_out, p_out, pB8_out, pB9_out, r_out, R_prime_T1_out, rB1_out, rB2_out,
       rB3_out, rB4_out, RT1_out, RT2_out;

  or or_1 (or_1_out, R_prime_T1_out, RT2_out, DR_prime_D6T6_out, rB4_out, rB3_out, rB2_out, rB1_out, pB9_out, pB8_out);
  not not_1 (not_1_out, E);
  not not_2 (not_2_out, R);
  PC pc_1 (.OUT(BUS_OUT), .CLR(RT1_out), .INC(or_1_out), .LD(or_2_out), .IN(BUS_IN), .CLK(CLK));
  and R_prime_T1 (R_prime_T1_out, not_2_out, SC[1]);
  and DR_prime_D6T6 (DR_prime_D6T6_out, nor_1_out, INS[6], SC[6]);
  and RT2 (RT2_out, R, SC[2]);
  nor nor_1 (nor_1_out, DR[0], DR[1], DR[2], DR[3], DR[4], DR[5], DR[6], DR[7], DR[8], DR[9], DR[10], DR[11], DR[12], DR[13], DR[14], DR[15]);
  and rB4 (rB4_out, ADDRESS[4], r_out, not_3_out);
  not not_3 (not_3_out, AC[15]);
  or or_2 (or_2_out, D4T4_out, D5T5_out);
  and rB3 (rB3_out, ADDRESS[3], r_out, AC[15]);
  and D4T4 (D4T4_out, SC[4], INS[4]);
  and D5T5 (D5T5_out, SC[5], INS[5]);
  and rB1 (rB1_out, r_out, ADDRESS[1], not_1_out);
  and rB2 (rB2_out, r_out, ADDRESS[2], nor_2_out);
  and pB9 (pB9_out, p_out, ADDRESS[9], FGI);
  and p (p_out, INS[7], SC[3], I);
  not not_4 (not_4_out, I);
  and pB8 (pB8_out, p_out, ADDRESS[8], FGO);
  and u_r (r_out, not_4_out, INS[7], SC[3]);
  and RT1 (RT1_out, R, SC[1]);
  nor nor_2 (nor_2_out, AC[0], AC[1], AC[2], AC[3], AC[4], AC[5], AC[6], AC[7], AC[8], AC[9], AC[10], AC[11], AC[12], AC[13], AC[14], AC[15]);
endmodule

// DR
module control_DR (
  input  [15:0] BUS_IN,
  input  CLK,
  input  [7:0] SC,
  input  [7:0] INS,
  output [15:0] BUS_OUT
);

  wire D0T4_out, D1T4_out, D2T4_out, D6T4_out, D6T5_out, or_1_out;

  and D6T5 (D6T5_out, INS[6], SC[5]);
  and D0T4 (D0T4_out, INS[0], SC[4]);
  and D1T4 (D1T4_out, INS[1], SC[4]);
  and D2T4 (D2T4_out, INS[2], SC[4]);
  and D6T4 (D6T4_out, INS[6], SC[4]);
  or or_1 (or_1_out, D0T4_out, D1T4_out, D2T4_out, D6T4_out);
  DR dr_1 (.BUS_IN(BUS_IN), .LD(or_1_out), .INC(D6T5_out), .CLK(CLK), .CLR(1'b0), .BUS_OUT(BUS_OUT));
endmodule

// TR
module control_TR (
  input  [15:0] BUS_IN,
  input  CLK,
  input  R,
  input  [7:0] SC,
  output [15:0] BUS_OUT
);

  wire and_1_out;

  and and_1 (and_1_out, R, SC[0]);
  TR tr_1 (.BUS_OUT(BUS_OUT), .BUS_IN(BUS_IN), .LD(and_1_out), .INC(1'b0), .CLK(CLK), .CLR(1'b0));
endmodule

// AC
module control_AC (
  input  CLK,
  input  [15:0] ALU_IN,
  input  [7:0] INS,
  input  [7:0] SC,
  input  [11:0] ADDRESS,
  input  I,
  output [15:0] BUS_OUT
);

  wire and_1_out, and_2_out, and_3_out, and_4_out, and_5_out, and_6_out, and_7_out, and_8_out, and_9_out,
       or_1_out, or_2_out, p_out, r_out;

  or or_1 (or_1_out, or_2_out, and_2_out);
  or or_2 (or_2_out, and_3_out, and_4_out, and_5_out, and_6_out, and_7_out, and_8_out, and_9_out);
  AC ac_1 (.ALU_IN(ALU_IN), .CLK(CLK), .CLR(and_1_out), .BUS_OUT(BUS_OUT), .INC(and_2_out), .LD(or_1_out));
  and and_1 (and_1_out, ADDRESS[11], r_out);
  and and_2 (and_2_out, r_out, ADDRESS[5]);
  and and_3 (and_3_out, INS[0], SC[5]);
  and and_4 (and_4_out, INS[1], SC[5]);
  and and_5 (and_5_out, INS[2], SC[5]);
  and and_6 (and_6_out, r_out, ADDRESS[9]);
  and and_7 (and_7_out, r_out, ADDRESS[7]);
  and and_8 (and_8_out, r_out, ADDRESS[6]);
  and and_9 (and_9_out, ADDRESS[11], p_out);
  and r (r_out, INS[7], SC[3], ~I);  // AND_Gate
  and p (p_out, INS[7], SC[3], I);
endmodule

module OUTR (
  input  [15:0] BUS_IN,
  input  [7:0] INS,
  input  CLK,
  input  [11:0] ADDRESS,
  input  [7:0] SC,
  input  I,
  output [7:0] OUT
);

  wire and_1_out, p_out;

  and p (p_out, INS[7], SC[3], I);
  and and_1 (and_1_out, ADDRESS[10], p_out);
  Register register_1 (.D(BUS_IN[7:0]), .en(and_1_out), .Q(OUT), .clk(CLK));  // open: clr
endmodule

module BUS (
  input  I,
  input  [7:0] INS,
  input  [7:0] SC,
  input  [11:0] ADDRESS,
  input  R,
  input  [15:0] AR,
  input  [15:0] PC,
  input  [15:0] DR,
  input  [15:0] AC,
  input  [15:0] IR,
  input  [15:0] TR,
  input  [15:0] Mem,
  output [15:0] BUS_OUT
);

  wire D0T4_out, D1T4_out, D2T4_out, D2T5_out, D3T4_out, D4T4_out, D5T4_out, D5T5_out, D6T4_out, D6T6_out,
       D7_prime_IT3_out, nor_1_out, not_1_out, not_2_out, not_3_out, or_1_out, or_2_out, or_3_out, or_4_out,
       or_5_out, p_out, pB10_out, r_out, R_prime_T1_out, R_prime_T2_out, rB6_out, rB7_out, RT1_out;
  wire [2:0] SELECT;

  not not_1 (not_1_out, R);
  not not_2 (not_2_out, I);
  not not_3 (not_3_out, INS[7]);
  and u_r (r_out, not_2_out, INS[7], SC[3]);
  and p (p_out, I, SC[3], INS[7]);
  and D4T4 (D4T4_out, INS[4], SC[4]);
  and D5T5 (D5T5_out, INS[5], SC[5]);
  and D5T4 (D5T4_out, INS[5], SC[4]);
  and D2T5 (D2T5_out, INS[2], SC[5]);
  and D6T6 (D6T6_out, INS[6], SC[6]);
  and D3T4 (D3T4_out, INS[3], SC[4]);
  and rB7 (rB7_out, r_out, ADDRESS[7]);
  and rB6 (rB6_out, r_out, ADDRESS[6]);
  and pB10 (pB10_out, p_out, ADDRESS[10]);
  and R_prime_T2 (R_prime_T2_out, not_1_out, SC[2]);
  and RT1 (RT1_out, SC[1], R);
  and R_prime_T1 (R_prime_T1_out, not_1_out, SC[1]);
  and D7_prime_IT3 (D7_prime_IT3_out, I, not_3_out, SC[3]);
  and D0T4 (D0T4_out, INS[0], SC[4]);
  and D1T4 (D1T4_out, SC[4], INS[1]);
  and D2T4 (D2T4_out, SC[4], INS[2]);
  and D6T4 (D6T4_out, SC[4], INS[6]);
  or or_1 (or_1_out, D4T4_out, D5T5_out);
  or or_2 (or_2_out, D5T4_out, SC[0]);
  or or_3 (or_3_out, D2T5_out, D6T6_out);
  or or_4 (or_4_out, D3T4_out, rB7_out, rB6_out, pB10_out);
  or or_5 (or_5_out, R_prime_T1_out, D7_prime_IT3_out, D0T4_out, D1T4_out, D2T4_out, D6T4_out);
  Multiplexer #(.select(3), .width(16), .enable("false")) multiplexer_1 (
    .in1(AR), .in2(PC), .in3(DR), .in4(AC), .in5(IR), .in6(TR), .in7(Mem), .out(BUS_OUT), .sel(SELECT));  // open: in0
  nor nor_1 (nor_1_out, or_5_out, RT1_out, R_prime_T2_out, or_4_out, or_3_out, or_2_out, or_1_out);
  Priority_Encoder priority_encoder_1 (
    .in0(nor_1_out), .in1(or_1_out), .in2(or_2_out), .in3(or_3_out), .in4(or_4_out), .in5(R_prime_T2_out),
    .in6(RT1_out), .in7(or_5_out), .out(SELECT));  // open: en_in, gs, en_out
endmodule

module R (
  input  FGO,
  input  FGI,
  input  IEN,
  input  CLK,
  input  [7:0] SC,
  output OUT
);

  wire and_1_out, not_1_out, not_2_out, not_3_out, or_1_out;

  or or_1 (or_1_out, FGO, FGI);
  not not_1 (not_1_out, SC[0]);
  not not_2 (not_2_out, SC[1]);
  not not_3 (not_3_out, SC[2]);
  and and_1 (and_1_out, or_1_out, IEN, not_1_out, not_2_out, not_3_out);
  J_K_Flip_Flop j_k_ff_1 (
    .J(and_1_out), .clk(CLK), .K(1'b0), .Q(OUT), .preset(1'b0), .en(1'b0), .reset(1'b0));  // open: Qn
endmodule

module E (
  input  CLK,
  input  Cout,
  input  [7:0] INS,
  input  [7:0] SC,
  input  [11:0] ADDRESS,
  input  I,
  output E
);

  wire and_2_out, and_3_out, and_4_out, and_5_out, and_6_out, d_ff_1_qn, multiplexer_1_out, or_1_out, r;

  and and_1 (r, INS[7], SC[3], ~I);  // AND_Gate
  and and_2 (and_2_out, r, ADDRESS[6]);
  and and_3 (and_3_out, r, ADDRESS[7]);
  and and_4 (and_4_out, r, ADDRESS[8]);
  and and_5 (and_5_out, INS[1], SC[5]);
  Multiplexer #(.enable("false")) multiplexer_1 (.in0(Cout), .in1(d_ff_1_qn), .out(multiplexer_1_out), .sel(and_4_out));
  or or_1 (or_1_out, and_2_out, and_3_out, and_4_out, and_5_out);
  D_Flip_Flop #(.trigger("falling")) d_ff_1 (
    .clk(CLK), .D(multiplexer_1_out), .Q(E), .Qn(d_ff_1_qn), .en(or_1_out), .reset(and_6_out));  // open: preset
  and and_6 (and_6_out, ADDRESS[10], r);
endmodule

module IEN (
  input  [7:0] INS,
  input  [7:0] SC,
  input  R,
  input  CLK,
  input  [11:0] ADDRESS,
  input  I,
  output OUT
);

  wire and_1_out, and_2_out, and_3_out, or_1_out, p_out;

  and p (p_out, INS[7], SC[3], I);
  and and_1 (and_1_out, R, SC[2]);
  and and_2 (and_2_out, ADDRESS[6], p_out);
  and and_3 (and_3_out, ADDRESS[7], p_out);
  or or_1 (or_1_out, and_1_out, and_2_out);
  J_K_Flip_Flop j_k_ff_1 (
    .J(and_3_out), .clk(CLK), .K(or_1_out), .Q(OUT), .preset(1'b0), .en(1'b0), .reset(1'b0));  // open: Qn
endmodule

module FGI (
  input  [7:0] INPR,
  input  [11:0] ADDRESS,
  input  CLK,
  input  [7:0] SC,
  input  [7:0] INS,
  input  I,
  output OUT
);

  wire and_1_out, or_1_out, p_out;

  and p (p_out, SC[3], I, INS[7]);
  and and_1 (and_1_out, ADDRESS[11], p_out);
  or or_1 (or_1_out, INPR[7], INPR[6], INPR[5], INPR[4], INPR[3], INPR[2], INPR[1], INPR[0]);
  J_K_Flip_Flop j_k_ff_1 (
    .J(or_1_out), .clk(CLK), .K(and_1_out), .Q(OUT), .preset(1'b0), .en(1'b0), .reset(1'b0));  // open: Qn
endmodule

module FGO (
  input  [11:0] ADDRESS,
  input  CLK,
  input  [7:0] INS,
  input  [7:0] SC,
  input  I,
  output OUT
);

  wire and_1_out;

  and and_1 (and_1_out, ADDRESS[7], SC[3], INS[7], I);
  J_K_Flip_Flop j_k_ff_1 (.J(SC[0]), .clk(CLK), .K(and_1_out), .Q(OUT));  // open: Qn, preset, en, reset
endmodule

// SC
module control_SC (
  input  R,
  input  CLK,
  input  [7:0] INS,
  output [7:0] SC
);

  wire D0T5_out, D1T5_out, D2T5_out, D3T4_out, D4T4_out, D5T5_out, D6T6_out, D7T3_out, or_1_out, RT2_out;

  Sequence_Counter sequence_counter_1 (.CLK(CLK), .CLR(or_1_out), .OUT(SC));
  and D7T3 (D7T3_out, SC[4], INS[7]);
  and RT2 (RT2_out, R, SC[3]);
  and D0T5 (D0T5_out, SC[6], INS[0]);
  and D1T5 (D1T5_out, SC[6], INS[1]);
  and D2T5 (D2T5_out, SC[6], INS[2]);
  and D3T4 (D3T4_out, SC[5], INS[3]);
  and D4T4 (D4T4_out, SC[5], INS[4]);
  and D5T5 (D5T5_out, SC[6], INS[5]);
  and D6T6 (D6T6_out, SC[7], INS[6]);
  or or_1 (or_1_out, 1'b0, D7T3_out, RT2_out, D0T5_out, D1T5_out, D2T5_out, D3T4_out, D4T4_out, D5T5_out, D6T6_out);

  // Other names for the same wires on the sheet: seq[7:0] = SC; T5 = SC[6]
endmodule

// Memory Control
module Memory (
  input  R,
  input  I,
  input  [7:0] SC,
  input  [7:0] INS,
  output out_5,
  output LD
);

  wire D0T4_out, D1T4_out, D2T4_out, D6T4_out, D7_prime_IT3_out, not_1_out, not_2_out, R_prime_T1_out,
       RT1_2_out, RT1_3_out, RT1_4_out, RT1_out;

  not not_1 (not_1_out, R);
  not not_2 (not_2_out, INS[7]);
  and RT1 (RT1_out, R, SC[1]);
  and RT1_2 (RT1_2_out, SC[4], INS[3]);
  and RT1_3 (RT1_3_out, SC[4], INS[5]);
  and RT1_4 (RT1_4_out, SC[6], INS[6]);
  and R_prime_T1 (R_prime_T1_out, not_1_out, SC[1]);
  and D7_prime_IT3 (D7_prime_IT3_out, not_2_out, SC[3], I);
  and D0T4 (D0T4_out, INS[0], SC[4]);
  and D1T4 (D1T4_out, INS[1], SC[4]);
  and D2T4 (D2T4_out, INS[2], SC[4]);
  and D6T4 (D6T4_out, INS[6], SC[4]);
  or or_1 (out_5, RT1_out, RT1_2_out, RT1_3_out, RT1_4_out);
  or or_2 (LD, R_prime_T1_out, D7_prime_IT3_out, D0T4_out, D1T4_out, D2T4_out, D6T4_out);

  // Other names for the same wires on the sheet: T4 = SC[4]
endmodule

module ALU (
  input  [7:0] INPR,
  input  E_IN,
  input  [15:0] AC,
  input  [15:0] DR,
  input  I,
  input  [7:0] SC,
  input  [7:0] INS,
  input  [11:0] ADDRESS,
  output [15:0] ALU_OUT,
  output ALU_Cout
);

  wire B6_out, B7_out, B9_out, B11_out, Cout, D0T5_out, D1T5_out, D2T5_out, E_L, E_R, nor_1_out, not_2_out,
       p, r;
  wire [2:0] Sel;
  wire [15:0] ACcomp, ACL, ACR, ADD, AND;

  _16_Bit_ADDER u_16_bit_adder_1 (.SUM(ADD), .B(DR), .A(AC), .Cin(1'b0), .Cout(Cout));
  Shift_Right shift_right_1 (.\input (AC), .E_IN(E_IN), .E_OUT(E_R), .OUT(ACR));
  Shift_Left shift_left_1 (.\input (AC), .OUT(ACL), .E_OUT(E_L), .E_IN(E_IN));
  assign AND = AC & DR;  // AND_Gate and_1, 16 bits wide
  assign ACcomp = ~AC;  // NOT_Gate not_1, 16 bits wide
  not not_2 (not_2_out, I);
  and and_2 (r, not_2_out, SC[3], INS[7]);
  and and_3 (p, I, SC[3], SC[3]);
  and B6 (B6_out, ADDRESS[6], r);
  and B7 (B7_out, ADDRESS[7], r);
  and B9 (B9_out, ADDRESS[9], r);
  and B11 (B11_out, ADDRESS[11], p);
  and D2T5 (D2T5_out, SC[5], INS[2]);
  and D1T5 (D1T5_out, SC[5], INS[1]);
  and D0T5 (D0T5_out, SC[5], INS[0]);
  nor nor_1 (nor_1_out, D0T5_out, D1T5_out, D2T5_out, B11_out, B9_out, B7_out, B6_out);
  // Priority_Encoder priority_encoder_1: pin names not known; wires that end beside it: nor_1_out, D0T5_out, D1T5_out, D2T5_out, Sel, B11_out, B9_out, B7_out, B6_out
  Multiplexer #(.select(3), .width(16), .enable("false")) multiplexer_1 (
    .in0(AC), .in1(AND), .in2(ADD), .in3(DR), .in4({{8{1'b0}}, INPR}), .in5(ACcomp), .in6(ACR), .in7(ACL),
    .out(ALU_OUT), .sel(Sel));
  Multiplexer #(.select(3), .enable("false")) multiplexer_2 (
    .in2(Cout), .in6(E_R), .in7(E_L), .out(ALU_Cout), .sel(Sel));  // open: in0, in1, in3, in4, in5

  // Other names for the same wires on the sheet: E = E_IN; INPR_t[7:0] = INPR
endmodule

// cirshr
module Shift_Right (
  input  [15:0] \input ,
  input  E_IN,
  output E_OUT,
  output [15:0] OUT
);

  Register #(.width(16), .trigger("high")) register_1 (
    .D({E_IN, \input [15:1]}), .Q(OUT), .clk(1'b1));  // open: en, clr

  assign E_OUT = \input [0];
endmodule

// cirshl
module Shift_Left (
  input  E_IN,
  input  [15:0] \input ,
  output [15:0] OUT,
  output E_OUT
);

  Register #(.width(16), .trigger("high")) register_1 (
    .D({\input [14:0], E_IN}), .Q(OUT), .clk(1'b1));  // open: en, clr

  assign E_OUT = \input [15];
endmodule
